# Fritzing sketch delay_switch_schmatic (saved by Fritzing 0.9.2b)
circuit board: 3.31532cm x 5.11832cm
breadboards: 1

parts:
  R2 = Resistor [tolerance=±5% resistance=1k package=THT]
  HLK-PM1 = HLK-PM01 [chip_label=HLK-PM01 package="DIP (Dual Inline) [THT]"]
  J1 = Screw terminal - 2 pins [package=THT]
  J2 = screw terminal, 3 pins
  SG1 = Buzzer 12mm [package=buzzer-12mm-ns]
  U1 = ATTINY45 [package=so]
  D1 = Rectifier Diode [part_number=1N4001 package="300 mil [THT]"]
  R1 = Resistor [tolerance=±5% resistance=10k package=THT]
  Q1 = NPN-Transistor [package="TO92 [THT]"]
  C1 = Electrolytic Capacitor [capacitance=0.1nF voltage=20V package="100 mil [THT, electrolytic]"]
  元件2 = songle relay

nets:
  N1: R2.Pin_0, U1.PB4(ADC2)
  N2: R2.Pin_1, Q1.B
  N3: HLK-PM1.AC-1, J2.pin3
  N4: HLK-PM1.AC-2, J2.pin1, 元件2.B
  N5: HLK-PM1.-Vo, U1.GND, R1.Pin_1, Q1.E
  N6: HLK-PM1.+Vo, J1.pin1, SG1.1, U1.VCC, D1.cathode, C1.+, 元件2.COIL1
  N7: J1.pin2, U1.PB1(MISO), R1.Pin_0, C1.-
  N8: J2.pin2, 元件2.CT
  N9: SG1.2, U1.PB0(MOSI)
  N10: D1.anode, Q1.C, 元件2.COIL2

custom parts:
  HLK-PM01: HiLink HLK-PM01 AC input: 100 ~ 240v , DC output: 5v
